# Fritzing sketch KISSRtwo (saved by Fritzing 0.9.9b)
circuit board: 4.99252cm x 4.16207cm
breadboards: 1

parts:
  T_ext = female pin header, 3 pins [form="♀ (female)" part_number="dallas 1"]
  Part6 = Radiometrix NTX2  # not connected
  J2 = female pin header, 4 pins [form="♀ (female)" part_number="ntx2 4-pin"]
  J3 = female pin header, 2 pins [form="♀ (female)" part_number="pro-mini a4/5"]
  J5 = female pin header, 4 pins [form="♀ (female)" part_number="pro-mini power"]
  J6 = female pin header, 6 pins [form="♀ (female)" part_number=openlog]
  J7 = female pin header, 4 pins [form="♀ (female)" part_number="i2c 4"]
  J8 = female pin header, 4 pins [form="♀ (female)" part_number="i2c 3"]
  J9 = female pin header, 4 pins [form="♀ (female)" part_number="i2c 2"]
  J10 = female pin header, 4 pins [form="♀ (female)" part_number="i2c 1"]
  JP1 = Header 2 [package=jst-2-pth-kit]
  J11 = female pin header, 4 pins [form="♀ (female)" part_number="pro-mini rx/tx"]
  J12 = female pin header, 4 pins [form="♀ (female)" part_number="pro-mini d6-d9"]
  J13 = female pin header, 4 pins [form="♀ (female)" part_number=ft232]
  J14 = female pin header, 3 pins [form="♀ (female)" part_number="ntx2 3-pin"]
  Part8 = Arduino Pro Mini v13  # not connected
  R2 = Resistor [tolerance=±5% resistance=220 power=0.25 package=THT]
  T_ext1 = female pin header, 3 pins [form="♀ (female)" part_number="dallas 1"]
  J15 = female pin header, 2 pins [form="♀ (female)" part_number="pro-mini a4/5"]  # not connected
  R3 = Resistor [tolerance=±5% resistance=220 power=0.25 package=THT]  # not connected
  J1 = female pin header, 7 pins [form="♀ (female)"]
  J$6 = SMA Antenna Connector [package=sma-edge]
  J4 = female pin header, 4 pins [form="♀ (female)"]  # not connected

nets (from the schematic view):
  N1: T_ext.pin1, J5.pin2, J7.pin2, J8.pin2, J9.pin2, J10.pin2, JP1.1, T_ext1.pin1
  N2: T_ext.pin2, R2.Pin_1, T_ext1.pin2
  N3: T_ext.pin3, J2.pin2, J5.pin1, J6.pin3, J7.pin1, J8.pin1, J9.pin1, J10.pin1, JP1.2, R2.Pin_0, T_ext1.pin3
  N4: J2.pin3, J6.pin1, J6.pin2, J11.pin4, J13.pin4
  N5: J2.pin4, J12.pin4
  N6: J3.pin1, J7.pin3, J8.pin3, J9.pin3, J10.pin3
  N7: J3.pin2, J7.pin4, J8.pin4, J9.pin4, J10.pin4
  N8: J5.pin4, J1.pin7
  N9: J6.pin4, J12.pin1
  N10: J6.pin5, J12.pin2, J13.pin3
  N11: J6.pin6, J12.pin3
  N12: J11.pin1, J1.pin4
  N13: J11.pin2, J1.pin3
  N14: J14.pin1, J14.pin3, J$6.GND
  N15: J14.pin2, J$6.SIGNAL

notes:
  VCC
  KISSR:two
  GND
  RAW
  TX
  RX
  D6
  D8
  D7
  GRN
  D11
  EN
  TXD
  D9
  DQ
  SCL
  SDA
  A5
  A4
  OpenLog
  I2C BUS
  D10
  OUT
  GPS
  DS18B20
  BLK
  FT232R
  NTX2B
  POWER
  LED
  +
  -

custom parts:
  Radiometrix NTX2: The NTX2 transmitter and NRX2 receiver offer a low power, reliable data link in a Radiometrix SIL standard pin out and foot print.
